// Logisim project CPU.circ as structural Verilog: 3 circuits, main circuit main
module main (
  input  Reset
);

  wire Clock_out, cpu_1_write_ram;
  wire [15:0] cpu_1_ram_address, cpu_1_ram_out, cpu_1_rom_address, ram_1_data, rom_1_data;

  Clock Clock (.out(Clock_out));
  CPU cpu_1 (
    .Reset(Reset), .ROM_address(cpu_1_rom_address), .RAM_address(cpu_1_ram_address), .Clock(Clock_out),
    .RAM_in(ram_1_data), .Write_RAM(cpu_1_write_ram), .RAM_out(cpu_1_ram_out), .ROM_in(rom_1_data));
  ROM #(.addrWidth(16), .dataWidth(16)) rom_1 (.addr(cpu_1_rom_address), .data(rom_1_data));  // open: sel
  RAM #(.addrWidth(16), .dataWidth(16), .bus("separate")) ram_1 (
    .addr(cpu_1_ram_address), .din(cpu_1_ram_out), .data(ram_1_data), .str(cpu_1_write_ram), .clk(Clock_out));  // open: sel, ld, clr

  // Notes on the sheet:
  //   RAM
  //   ROM
endmodule

module CPU (
  input  Reset,
  input  Clock,
  input  [15:0] ROM_in,
  input  [15:0] RAM_in,
  output [15:0] ROM_address,
  output [15:0] RAM_address,
  output [15:0] RAM_out,
  output Write_RAM
);

  wire alu_1_ng, alu_1_zr, and_1_out, and_2_out, and_4_out, and_5_out, and_6_out, nor_1_out, not_1_out,
       not_2_out, or_1_out, or_2_out;
  wire [15:0] D_q, multiplexer_1_out, multiplexer_2_out;

  // Probe on ROM_in
  // Probe on RAM_in
  not not_1 (not_1_out, ROM_in[15]);
  Multiplexer #(.width(16), .enable("false")) multiplexer_1 (
    .in0(RAM_address), .in1(RAM_in), .out(multiplexer_1_out), .sel(ROM_in[12]));
  or or_1 (or_1_out, not_1_out, ROM_in[5]);
  and and_1 (and_1_out, or_2_out, ROM_in[15]);
  and and_2 (and_2_out, ROM_in[15], ROM_in[4]);
  and and_3 (Write_RAM, ROM_in[15], ROM_in[3]);
  ALU alu_1 (
    .nx(ROM_in[10]), .out(RAM_out), .x(D_q), .f(ROM_in[7]), .zr(alu_1_zr), .y(multiplexer_1_out),
    .ny(ROM_in[8]), .ng(alu_1_ng), .zx(ROM_in[11]), .zy(ROM_in[9]), .no(ROM_in[6]));
  not not_2 (not_2_out, and_1_out);
  Multiplexer #(.width(16), .enable("false")) multiplexer_2 (
    .in0(ROM_in), .in1(RAM_out), .out(multiplexer_2_out), .sel(ROM_in[15]));
  nor nor_1 (nor_1_out, alu_1_zr, alu_1_ng);
  Counter #(.width(16), .max('hffff)) PC (
    .load(and_1_out), .D(RAM_address), .count(not_2_out), .Q(ROM_address), .clk(Clock), .clr(Reset));  // open: carry
  Register #(.width(16)) A (.D(multiplexer_2_out), .en(or_1_out), .Q(RAM_address), .clk(Clock), .clr(Reset));
  Register #(.width(16)) D (.D(RAM_out), .en(and_2_out), .Q(D_q), .clk(Clock), .clr(Reset));
  and and_4 (and_4_out, alu_1_ng, ROM_in[2]);
  and and_5 (and_5_out, alu_1_zr, ROM_in[1]);
  and and_6 (and_6_out, nor_1_out, ROM_in[0]);
  or or_2 (or_2_out, and_4_out, and_5_out, and_6_out);
  // Probe on ROM_address
  // Probe on RAM_address
  // Probe on RAM_out
endmodule

module ALU (
  input  [15:0] x,
  input  [15:0] y,
  input  zx,
  input  nx,
  input  zy,
  input  ny,
  input  f,
  input  no,
  output [15:0] out,
  output zr,
  output ng
);

  wire [15:0] adder_1_out, and_1_out, multiplexer_1_out, multiplexer_2_out, multiplexer_3_out,
       multiplexer_4_out, multiplexer_5_out, not_1_out, not_2_out, not_3_out;

  Multiplexer #(.width(16), .enable("false")) multiplexer_1 (
    .in0(x), .in1({16{1'b0}}), .out(multiplexer_1_out), .sel(zx));
  assign not_1_out = ~multiplexer_1_out;  // NOT_Gate not_1, 16 bits wide
  Multiplexer #(.width(16), .enable("false")) multiplexer_2 (
    .in0(multiplexer_1_out), .in1(not_1_out), .out(multiplexer_2_out), .sel(nx));
  Multiplexer #(.width(16), .enable("false")) multiplexer_3 (
    .in0(y), .in1({16{1'b0}}), .out(multiplexer_3_out), .sel(zy));
  assign not_2_out = ~multiplexer_3_out;  // NOT_Gate not_2, 16 bits wide
  Multiplexer #(.width(16), .enable("false")) multiplexer_4 (
    .in0(multiplexer_3_out), .in1(not_2_out), .out(multiplexer_4_out), .sel(ny));
  assign and_1_out = multiplexer_2_out & multiplexer_4_out;  // AND_Gate and_1, 16 bits wide
  Multiplexer #(.width(16), .enable("false")) multiplexer_5 (
    .in0(and_1_out), .in1(adder_1_out), .out(multiplexer_5_out), .sel(f));
  Adder #(.width(16)) adder_1 (.a(multiplexer_2_out), .b(multiplexer_4_out), .out(adder_1_out));  // open: cin, cout
  assign not_3_out = ~multiplexer_5_out;  // NOT_Gate not_3, 16 bits wide
  Multiplexer #(.width(16), .enable("false")) multiplexer_6 (
    .in0(multiplexer_5_out), .in1(not_3_out), .out(out), .sel(no));
  Comparator #(.width(16)) comparator_1 (.a(out), .b({16{1'b0}}), .eq(zr), .lt(ng));  // open: gt
endmodule
